# Fritzing sketch pre-bluetooth-v1 (saved by Fritzing 0.9.10b)

parts:
  U1 = HALL-EFFECT [package=sc70]
  U2 = HALL-EFFECT [package=sc70]
  U3 = HALL-EFFECT [package=sc70]
  Mod1 = Raspberry Pi Pico
  Part1 = 9-DOF IMU L3GD20H + LSM303 [part_number=1714]
  S1 = Pushbutton [package="[THT]"]

nets:
  GND: U1.GND, U2.GND, U3.GND, Mod1.pin_8, Mod1.pin_13, Mod1.pin_18, Mod1.pin_23, Mod1.pin_28, Mod1.pin_38, Part1.GND, S1.Pin_1, S1.Pin_2
  VCC: U1.VCC, U2.VCC, U3.VCC, Mod1.pin_36, Part1.VIN
  N1: U1.OUT, Mod1.pin_31
  N2: U2.OUT, Mod1.pin_32
  N3: U3.OUT, Mod1.pin_34
  N4: Mod1.pin_7, S1.Pin_3, S1.Pin_4
  N5: Mod1.pin_26, Part1.SDA
  N6: Mod1.pin_27, Part1.SCL

custom parts:
  Raspberry Pi Pico: Raspberry Pi Pico. Based around the RP2040 microcontroller the Pico is a low cost microcontroller device bringing Raspberry Pi quality, cost, and easy of use to the microcontroller space. Jan 2021, Split part in to two versions: tht (this one) and SMD. This one will drill holes for a .1 in header in pcb to allow plugging in the module as well as providing pads to solder the module to the top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
  9-DOF IMU L3GD20H + LSM303: This inertial-measurement-unit combines 2 of the best quality sensors available on the market to give you 9 axes of data: 3 axes of accelerometer data, 3 axes gyroscopic, and 3 axes magnetic (compass). We tested many different 'combination' sensors and found these were the best value, with stable and reliable readings.
